# Fritzing sketch capston (saved by Fritzing 0.9.3b)

parts:
  A1 = u-blox NEO-6M GPS Breakout
  U2 = ESP8266 NodeMCU LoLin module
  LCD1 = TFT 1.8 inch 160x128 w SD
  BAT1 = 18650 battery holder [package=battery-18650-kit]
  LED1 = LED - 5mm [color="Red (633nm)" package="5 mm [THT]"]
  LED2 = Green LED - Rect 5x2x7mm [package="5x2x7 mm [THT]"]
  LED3 = LEDs [package=led10mm]
  U3 = SWITCH_SPDT [package=kps-1290]
  S5 = Pushbutton [package=THT]
  MS1 = MS5611
  GY1 = MPU-6050 Board GY-521 [form="♀ (female)" package=THT]
  TP1 = TP4056 [chip_label=TP4056 package="DIP (Dual Inline) [THT]"]
  J1 = Piezo Speaker

nets:
  3V3: A1.Pin_1, U2.3V3, LCD1.pin_1, LCD1.pin4, LCD1.pin_8, S5.leg1, MS1.VIN, GY1.pin1
  GND: A1.Pin_2, U2.GND, LCD1.pin2, LED1.cathode, LED2.cathode, LED3.A, MS1.GND, GY1.pin2, J1.pin1
  N1: A1.Pin_3, U2.TX
  N2: A1.Pin_4, U2.RX
  N3: U2.D0, J1.pin2
  N4: U2.D1, MS1.SCL, GY1.pin3
  N5: U2.D2, MS1.SDA, GY1.pin4
  N6: U2.D4, LCD1.pin_5
  N7: U2.D5, LCD1.pin_7
  N8: U2.D6, S5.leg0
  N9: U2.D7, LCD1.pin_6
  N10: U2.D8, LCD1.pin3
  N11: U2.Vin, U3.O
  N12: U2.S1, LED3.C
  N13: U2.S2, LED2.anode
  N14: U2.S3, LED1.anode
  N15: BAT1.+, TP1.pin4
  N16: BAT1.-, TP1.pin5
  N17: U3.P, TP1.pin3

custom parts:
  ESP8266 NodeMCU LoLin module: ESP8266 based NodeMCU
  TFT 1.8 inch 160x128 w SD: This is a generic 1.8 tft spi lcd display available on ebay and others. The 1.8" display has 128x160 color pixels.
  18650 battery holder: 18650 Battery Holder identical to the dual battery version.
  Green LED - Rect 5x2x7mm: A generic rectangular green LED (~1.8V) 5mm x 2mm x 7mm
  MPU-6050 Board GY-521: Acelerometro y Giroscopio MPU-6050 Board GY-521
  TP4056: A DIP stand-in part for whatever IC you want. With 6 pins on a 300mil dual inline package (DIP) footprint.
